// Logisim project circuitos_secuenciales.circ as structural Verilog: 14 circuits, main circuit ej_16_registroSimple
module aux_17_extensorSigno (
  input  i3,
  input  i2,
  input  i1,
  input  i0,
  input  ext,
  output o3,
  output o2,
  output o1,
  output o0
);

  wire and_1_out, and_2_out, and_3_out, and_4_out, not_1_out, not_2_out;

  not not_1 (not_1_out, ext);
  not not_2 (not_2_out, ext);
  and and_1 (and_1_out, not_1_out, i3);
  and and_2 (and_2_out, ext, i1);
  and and_3 (and_3_out, i1, ext);
  and and_4 (and_4_out, not_2_out, i2);
  or or_1 (o3, and_1_out, and_2_out);
  or or_2 (o2, and_3_out, and_4_out);

  assign o0 = i0;
  assign o1 = i1;
endmodule

module aux_17_extensorSignoSimple (
  input  i3,
  input  i2,
  input  i1,
  input  i0,
  input  ext,
  output o3,
  output o2,
  output o1,
  output o0
);

  Multiplexer multiplexer_1 (.in0(i2), .in1(i1), .out(o2), .sel(ext));
  Multiplexer multiplexer_2 (.in0(i3), .in1(i1), .out(o3), .sel(ext));

  assign o0 = i0;
  assign o1 = i1;
endmodule

module aux_18_salidaRegistrida (
  input  i0,
  input  i1,
  input  i2,
  input  i3,
  input  rd,
  output s0,
  output s1,
  output s2,
  output s3
);

  Multiplexer multiplexer_1 (.in0(s1), .in1(i0), .out(s0), .sel(rd));
  Multiplexer multiplexer_2 (.in0(s1), .in1(i3), .out(s3), .sel(rd));
  aux_18_siempreZero aux_18_siemprezero_1 (.i0(i1), .i1(i3), .s0(s1));

  assign s2 = s1;
endmodule

module aux_18_siempreZero (
  input  i0,
  input  i1,
  output s0
);

  and and_1 (s0, i1, 1'b0);
  and and_2 (s0, i0, 1'b0);
endmodule

module aux_19_bi_direccion (
  input  d3,
  input  s3,
  input  d2,
  input  s2,
  input  d1,
  input  s1,
  input  d0,
  input  s0,
  input  rd,
  output e0,
  output e1,
  output e2,
  output e3
);

  Multiplexer multiplexer_1 (.in0(d3), .in1(s3), .out(e3), .sel(rd));
  Multiplexer multiplexer_2 (.in0(d1), .in1(s1), .out(e1), .sel(rd));
  Multiplexer multiplexer_3 (.in0(d2), .in1(s2), .out(e2), .sel(rd));
  Multiplexer multiplexer_4 (.in0(d0), .in1(s0), .out(e0), .sel(rd));
endmodule

module aux_19_tresEstados (
  input  e0,
  input  e1,
  input  e2,
  input  e3,
  input  rd,
  output s3,
  output s2,
  output s1,
  output s0
);

  assign s0 = rd ? e0 : 1'bz;  // Controlled_Buffer controlled_buffer_1
  assign s1 = rd ? e1 : 1'bz;  // Controlled_Buffer controlled_buffer_2
  assign s3 = rd ? e3 : 1'bz;  // Controlled_Buffer controlled_buffer_3
  assign s2 = rd ? e2 : 1'bz;  // Controlled_Buffer controlled_buffer_4
endmodule

module otro_16_registroSimple (
  input  i0,
  input  i1,
  input  i2,
  input  i3,
  input  ld,
  output s0,
  output s1,
  output s2,
  output s3
);

  wire and_1_out, and_2_out, and_3_out, and_4_out, and_5_out, and_6_out, and_7_out, and_8_out, clock_1_out,
       not_1_out, not_2_out, not_3_out, not_4_out, or_1_out, or_2_out, or_3_out, or_4_out;

  Clock clock_1 (.out(clock_1_out));
  not not_1 (not_1_out, ld);
  not not_2 (not_2_out, ld);
  not not_3 (not_3_out, ld);
  not not_4 (not_4_out, ld);
  and and_1 (and_1_out, ld, i0);
  and and_2 (and_2_out, not_1_out, s0);
  and and_3 (and_3_out, ld, i1);
  and and_4 (and_4_out, not_2_out, s1);
  and and_5 (and_5_out, ld, i1);
  and and_6 (and_6_out, not_3_out, s2);
  and and_7 (and_7_out, ld, i1);
  and and_8 (and_8_out, not_4_out, s3);
  or or_1 (or_1_out, and_1_out, and_2_out);
  or or_2 (or_2_out, and_3_out, and_4_out);
  or or_3 (or_3_out, and_5_out, and_6_out);
  or or_4 (or_4_out, and_7_out, and_8_out);
  D_Flip_Flop d_ff_1 (.D(or_1_out), .clk(clock_1_out), .Q(s0));  // open: Qn, preset, reset
  D_Flip_Flop d_ff_2 (.D(or_2_out), .clk(clock_1_out), .Q(s1));  // open: Qn, preset, reset
  D_Flip_Flop d_ff_3 (.D(or_3_out), .clk(clock_1_out), .Q(s2));  // open: Qn, preset, reset
  D_Flip_Flop d_ff_4 (.D(or_4_out), .clk(clock_1_out), .Q(s3));  // open: Qn, preset, reset
endmodule

module otro_19_RegistroBidirecional (
  input  d3,
  input  d2,
  input  d1,
  input  d0,
  input  clk,
  input  ld,
  input  rd
);

  wire d_ff_1_q;
  wire [3:0] ej_16_registrosimple_1_s0;

  D_Flip_Flop d_ff_1 (.D(rd), .clk(clk), .Q(d_ff_1_q));  // open: Qn, preset, reset
  ej_16_registroSimple ej_16_registrosimple_1 (
    .i0(d0), .i1(d1), .i2(d2), .i3(d3), .clk(clk), .ld(ld), .s0(ej_16_registrosimple_1_s0[0]),
    .s1(ej_16_registrosimple_1_s0[1]), .s2(ej_16_registrosimple_1_s0[2]), .s3(ej_16_registrosimple_1_s0[3]));
  assign {d0, d1, d2, d3} = d_ff_1_q ? ej_16_registrosimple_1_s0 : 4'bz;  // Controlled_Buffer controlled_buffer_1
endmodule

module otro_18_registroSalidaRestringido (
  input  i0,
  input  i1,
  input  i2,
  input  i3,
  input  ld,
  input  clk,
  input  rd,
  output s0,
  output s1,
  output s2,
  output s3
);

  wire aux_18_siemprezero_1_s0, multiplexer_1_out, multiplexer_2_out;

  Multiplexer multiplexer_1 (.in0(i0), .in1(aux_18_siemprezero_1_s0), .out(multiplexer_1_out), .sel(rd));
  Multiplexer multiplexer_2 (.in0(i3), .in1(aux_18_siemprezero_1_s0), .out(multiplexer_2_out), .sel(rd));
  aux_18_siempreZero aux_18_siemprezero_1 (.i0(i1), .i1(i3), .s0(aux_18_siemprezero_1_s0));
  ej_16_registroSimple ej_16_registrosimple_1 (
    .i0(multiplexer_1_out), .i1(aux_18_siemprezero_1_s0), .i2(aux_18_siemprezero_1_s0),
    .i3(multiplexer_2_out), .clk(clk), .ld(ld), .s0(s0), .s1(s1), .s2(s2), .s3(s3));
endmodule

module ej_16_registroSimple (
  input  i0,
  input  i1,
  input  i2,
  input  i3,
  input  clk,
  input  ld,
  output s0,
  output s1,
  output s2,
  output s3
);

  wire and_1_out;

  and and_1 (and_1_out, clk, ld);
  D_Flip_Flop d_ff_1 (.D(i0), .clk(and_1_out), .Q(s0));  // open: Qn, preset, reset
  D_Flip_Flop d_ff_2 (.D(i1), .clk(and_1_out), .Q(s1));  // open: Qn, preset, reset
  D_Flip_Flop d_ff_3 (.D(i2), .clk(and_1_out), .Q(s2));  // open: Qn, preset, reset
  D_Flip_Flop d_ff_4 (.D(i3), .clk(and_1_out), .Q(s3));  // open: Qn, preset, reset
endmodule

module ej_17_extensorDeSigno (
  input  i3,
  input  i2,
  input  i1,
  input  i0,
  input  clk,
  input  ld,
  input  ext,
  output o0,
  output o1,
  output o2,
  output o3
);

  wire registroSimple_s0, registroSimple_s1, registroSimple_s2, registroSimple_s3;

  ej_16_registroSimple registroSimple (
    .i0(i0), .i1(i1), .i2(i2), .i3(i3), .clk(clk), .ld(ld), .s0(registroSimple_s0), .s1(registroSimple_s1),
    .s2(registroSimple_s2), .s3(registroSimple_s3));
  aux_17_extensorSignoSimple extensorSigno (
    .i3(registroSimple_s0), .i2(registroSimple_s1), .i1(registroSimple_s2), .i0(registroSimple_s3),
    .ext(ext), .o3(o3), .o2(o2), .o1(o1), .o0(o0));
endmodule

module ej_18_RegistroSalidaRestringidaSimple (
  input  i0,
  input  i1,
  input  i2,
  input  i3,
  input  clk,
  input  ld,
  input  rd,
  output s0,
  output s1,
  output s2,
  output s3
);

  wire salidaRestringida_s0, salidaRestringida_s1, salidaRestringida_s2, salidaRestringida_s3;

  aux_18_salidaRegistrida salidaRestringida (
    .i0(i0), .i1(i1), .i2(i2), .i3(i3), .rd(rd), .s0(salidaRestringida_s0), .s1(salidaRestringida_s1),
    .s2(salidaRestringida_s2), .s3(salidaRestringida_s3));
  ej_16_registroSimple registroSimple (
    .i0(salidaRestringida_s0), .i1(salidaRestringida_s1), .i2(salidaRestringida_s2),
    .i3(salidaRestringida_s3), .clk(clk), .ld(ld), .s0(s0), .s1(s1), .s2(s2), .s3(s3));
endmodule

module ej_19_RegistroBidirecional (
  input  clk,
  input  ld,
  input  rd,
  input  d0,
  input  d1,
  input  d2,
  input  d3
);

  wire d_ff_1_q, ej_16_registrosimple_1_s0, ej_16_registrosimple_1_s1, ej_16_registrosimple_1_s2,
       ej_16_registrosimple_1_s3, entradaRegistringida_s0, entradaRegistringida_s1, entradaRegistringida_s2,
       entradaRegistringida_s3, not_1_out;

  D_Flip_Flop d_ff_1 (.D(rd), .clk(clk), .Q(d_ff_1_q));  // open: Qn, preset, reset
  not not_1 (not_1_out, d_ff_1_q);
  ej_16_registroSimple ej_16_registrosimple_1 (
    .i0(entradaRegistringida_s0), .i1(entradaRegistringida_s1), .i2(entradaRegistringida_s2),
    .i3(entradaRegistringida_s3), .clk(clk), .ld(ld), .s0(ej_16_registrosimple_1_s0),
    .s1(ej_16_registrosimple_1_s1), .s2(ej_16_registrosimple_1_s2), .s3(ej_16_registrosimple_1_s3));
  aux_19_tresEstados entradaRegistringida (
    .e0(d3), .e1(d2), .e2(d1), .e3(d0), .rd(not_1_out), .s3(entradaRegistringida_s3),
    .s2(entradaRegistringida_s2), .s1(entradaRegistringida_s1), .s0(entradaRegistringida_s0));
  aux_19_tresEstados salidaRestringida (
    .e0(ej_16_registrosimple_1_s0), .e1(ej_16_registrosimple_1_s1), .e2(ej_16_registrosimple_1_s2),
    .e3(ej_16_registrosimple_1_s3), .rd(d_ff_1_q), .s3(entradaRegistringida_s3),
    .s2(entradaRegistringida_s2), .s1(entradaRegistringida_s1), .s0(entradaRegistringida_s0));
endmodule

module ej_20_ALU (
  input  add,
  input  sub,
  input  andd,
  input  orr,
  output V,
  output Z,
  output C,
  output N
);

  ej_16_registroSimple ej_16_registrosimple_1 ();  // open: i0, i1, i2, i3, clk, ld, s0, s1, s2, s3
  ej_16_registroSimple ej_16_registrosimple_2 ();  // open: i0, i1, i2, i3, clk, ld, s0, s1, s2, s3
endmodule
