// Logisim project circuitos_combinatorios.circ as structural Verilog
module aux (
  input  in_1,
  input  in_2,
  input  in_3,
  output out_4
);

  and and_1 (out_4, in_1, in_3);

  assign in_2 = in_1;
endmodule

module aux_12_comparadorCero (
  input  [3:0] E,
  output S
);

  wire or_1_out, or_2_out, or_3_out;

  or or_1 (or_1_out, E[0], E[1]);
  or or_2 (or_2_out, E[2], E[3]);
  or or_3 (or_3_out, or_1_out, or_2_out);
  not not_1 (S, or_3_out);
endmodule

module ej6 (
  input  C,
  input  B,
  input  A,
  output out_4
);

  wire and_1_out, and_2_out, not_1_out, or_1_out;

  not not_1 (not_1_out, B);
  and and_1 (and_1_out, C, B);
  and and_2 (and_2_out, not_1_out, A);
  or or_1 (or_1_out, and_1_out, and_2_out);
endmodule

module ej4 (
  input  A,
  input  B,
  input  C,
  output out_4,
  output out_5
);

  wire nand_1_out, nand_2_out;

  nand nand_1 (nand_1_out, A, B);
  nand nand_2 (nand_2_out, C, C);
  nand nand_3 (out_4, nand_1_out, nand_1_out);
endmodule

module ej5 (
  input  A,
  input  B,
  input  C,
  output out_4
);

  wire and_1_out, nor_1_out, nor_2_out, not_1_out, not_2_out, not_3_out, not_4_out;

  not not_1 (not_1_out, A);
  not not_2 (not_2_out, B);
  not not_3 (not_3_out, C);
  and and_1 (and_1_out, not_1_out, not_2_out);
  nor nor_1 (nor_1_out, and_1_out, not_3_out);
  not not_4 (not_4_out, nor_1_out);
  nor nor_2 (nor_2_out, not_4_out, not_4_out);
endmodule

module ej_7_demultiplexor_bis (
  input  e0,
  input  c0,
  input  c1,
  output s0,
  output s1,
  output s2,
  output s3
);

  wire and_1_out, and_2_out, and_3_out, and_4_out, not_1_out, not_2_out;

  not not_1 (not_1_out, c0);
  not not_2 (not_2_out, c1);
  and and_1 (and_1_out, not_1_out, not_2_out);
  and and_2 (and_2_out, not_1_out, c1);
  and and_3 (and_3_out, c0, not_2_out);
  and and_4 (and_4_out, c0, c1);
  and and_5 (s0, and_1_out, e0);
  and and_6 (s1, and_2_out, e0);
  and and_7 (s2, and_3_out, e0);
  and and_8 (s3, and_4_out, e0);
endmodule

module ej_7_demultiplexor (
  input  c0,
  input  c1,
  input  e0,
  output [3:0] S,
  output s0,
  output s1,
  output s2,
  output s3
);

  wire and_1_out, and_2_out, and_3_out, and_4_out, not_1_out, not_2_out, not_3_out, not_4_out;

  not not_1 (not_1_out, c0);
  not not_2 (not_2_out, c1);
  not not_3 (not_3_out, c0);
  not not_4 (not_4_out, c1);
  and and_1 (and_1_out, not_1_out, not_2_out);
  and and_2 (and_2_out, not_3_out, c1);
  and and_3 (and_3_out, c0, not_4_out);
  and and_4 (and_4_out, c0, c1);
  and and_5 (s0, and_1_out, e0);
  and and_6 (s1, and_2_out, e0);
  and and_7 (s2, and_3_out, e0);
  and and_8 (s3, and_4_out, e0);
endmodule

module ej_8_codificador (
  input  e3,
  input  e2,
  input  e1,
  input  e0,
  output s1,
  output s0
);

  wire nor_1_out, nor_2_out, xor_1_out, xor_2_out;

  nor nor_1 (nor_1_out, e0, e2);
  xor xor_1 (xor_1_out, e1, e3);
  nor nor_2 (nor_2_out, e0, e1);
  xor xor_2 (xor_2_out, e2, e3);
  and and_1 (s1, nor_1_out, xor_1_out);
  and and_2 (s0, nor_2_out, xor_2_out);
endmodule

module ej_9_codificador (
  input  e0,
  input  e1,
  output s0,
  output s1,
  output s2,
  output s3
);

  wire not_1_out, not_2_out, not_3_out, not_4_out;

  not not_1 (not_1_out, e0);
  not not_2 (not_2_out, e1);
  not not_3 (not_3_out, e0);
  not not_4 (not_4_out, e1);
  and and_1 (s0, not_1_out, not_2_out);
  and and_2 (s1, not_3_out, e1);
  and and_3 (s2, e0, not_4_out);
  and and_4 (s3, e0, e1);
endmodule

module ej_9_demuConCod (
  input  c1,
  input  c0,
  input  e0,
  output out_4,
  output out_5,
  output out_6,
  output out_7
);

  wire ej_9_codificador_1_s0, ej_9_codificador_1_s1, ej_9_codificador_1_s2, ej_9_codificador_1_s3;

  ej_9_codificador ej_9_codificador_1 (
    .e0(c0), .e1(c1), .s0(ej_9_codificador_1_s0), .s1(ej_9_codificador_1_s1), .s2(ej_9_codificador_1_s2),
    .s3(ej_9_codificador_1_s3));
  and and_1 (out_4, ej_9_codificador_1_s0, e0);
  and and_2 (out_5, ej_9_codificador_1_s1, e0);
  and and_3 (out_6, ej_9_codificador_1_s2, e0);
  and and_4 (out_7, ej_9_codificador_1_s3, e0);
endmodule

module ej_11a_sumadorCompleto (
  input  Cin,
  input  B,
  input  A,
  output Res,
  output Cout
);

  wire and_1_out, and_2_out, and_3_out, nor_1_out, or_1_out, xor_1_out;

  xor xor_1 (xor_1_out, A, B);
  nor nor_1 (nor_1_out, A, B);
  and and_1 (and_1_out, A, B);
  or or_1 (or_1_out, nor_1_out, and_1_out);
  and and_2 (and_2_out, Cin, or_1_out);
  and and_3 (and_3_out, Cin, xor_1_out);
  or or_2 (Res, xor_1_out, and_2_out);
  or or_3 (Cout, and_3_out, and_1_out);
endmodule

module ej_12a_sumadorCompleto4bits (
  input  Cin,
  input  [3:0] A,
  input  [3:0] B,
  output s0,
  output s1,
  output s2,
  output s3,
  output Cout
);

  wire ej_11a_sumadorcompleto_1_cout, ej_11a_sumadorcompleto_2_cout, ej_11a_sumadorcompleto_3_cout;

  ej_11a_sumadorCompleto ej_11a_sumadorcompleto_1 (
    .Cin(Cin), .B(A[0]), .A(B[0]), .Res(s0), .Cout(ej_11a_sumadorcompleto_1_cout));
  ej_11a_sumadorCompleto ej_11a_sumadorcompleto_2 (
    .Cin(ej_11a_sumadorcompleto_1_cout), .B(A[1]), .A(B[1]), .Res(s1), .Cout(ej_11a_sumadorcompleto_2_cout));
  ej_11a_sumadorCompleto ej_11a_sumadorcompleto_3 (
    .Cin(ej_11a_sumadorcompleto_2_cout), .B(A[2]), .A(B[2]), .Res(s2), .Cout(ej_11a_sumadorcompleto_3_cout));
  ej_11a_sumadorCompleto ej_11a_sumadorcompleto_4 (
    .Cin(ej_11a_sumadorcompleto_3_cout), .B(A[3]), .A(B[3]), .Res(s3), .Cout(Cout));
endmodule

module ej_12b_sumadorConFlags (
  input  [3:0] A,
  input  [3:0] B,
  input  Cin,
  output N,
  output C,
  output Z,
  output V
);

  wire [2:0] sumadorCompleto_s0;

  ej_12a_sumadorCompleto4bits sumadorCompleto (
    .Cin(Cin), .A(B), .B(A), .s0(sumadorCompleto_s0[0]), .s1(sumadorCompleto_s0[1]),
    .s2(sumadorCompleto_s0[2]), .s3(N), .Cout(C));
  aux_12_comparadorCero comparadorCero (.E({N, sumadorCompleto_s0}), .S(Z));
  nor nor_1 (V, N, A[3]);
endmodule

module ej_13b_inversoAditivo (
  input  e0,
  input  e1,
  input  e2,
  input  e3,
  input  [3:0] in_5,
  output s3,
  output s2,
  output s1,
  output s0
);

  wire [3:0] not_1_out;

  not not_1 (not_1_out[0], e3);
  not not_2 (not_1_out[1], e2);
  not not_3 (not_1_out[2], e1);
  not not_4 (not_1_out[3], e0);
  ej_12a_sumadorCompleto4bits ej_12a_sumadorcompleto4bits_1 (
    .A(not_1_out), .B(in_5), .s0(s3), .s1(s2), .s2(s1), .s3(s0));  // open: Cin, Cout
endmodule

module ej_13c_noTieneInv (
  input  [3:0] in_1,
  output out_2
);

  wire and_1_out, and_2_out, ej_13b_inversoaditivo_1_s0, ej_13b_inversoaditivo_1_s1,
       ej_13b_inversoaditivo_1_s2, ej_13b_inversoaditivo_1_s3, nor_1_out, nor_2_out, nor_3_out, nor_4_out;

  ej_13b_inversoAditivo ej_13b_inversoaditivo_1 (
    .e0(in_1[0]), .e1(in_1[1]), .e2(in_1[2]), .e3(in_1[3]), .s3(ej_13b_inversoaditivo_1_s3),
    .s2(ej_13b_inversoaditivo_1_s2), .s1(ej_13b_inversoaditivo_1_s1), .s0(ej_13b_inversoaditivo_1_s0));  // open: in_5
  nor nor_1 (nor_1_out, ej_13b_inversoaditivo_1_s0, in_1[0]);
  nor nor_2 (nor_2_out, ej_13b_inversoaditivo_1_s1, in_1[1]);
  nor nor_3 (nor_3_out, ej_13b_inversoaditivo_1_s2, in_1[2]);
  and and_1 (and_1_out, nor_2_out, nor_1_out);
  and and_2 (and_2_out, nor_3_out, and_1_out);
  nor nor_4 (nor_4_out, ej_13b_inversoaditivo_1_s3, in_1[3]);
  and and_3 (out_2, nor_4_out, and_2_out);
endmodule
